# Fritzing sketch DHT11 (saved by Fritzing 0.9.3b)
breadboards: 1

parts:
  DHT1 = DHT11 Humitidy and Temperature Sensor
  R4 = Resistor [tolerance=±5% resistance=10k package=THT]
  part = Resistor [tolerance=±5% resistance=220 package=THT]  # not connected
  Arduino1 = Arduino Uno (Rev3)

nets:
  VDD: DHT1.VDD, R4.Pin_0, Arduino1.5V
  N1: DHT1.DATA, R4.Pin_1, Arduino1.D8
  GND: DHT1.GND, Arduino1.GND

custom parts:
  DHT11 Humitidy and Temperature Sensor: DHT11 Humidity and Temperature Sensor
