# Fritzing sketch PullDownBtn_LED (saved by Fritzing 0.9.3b)
breadboards: 1

parts:
  Part2 = Arduino Uno (Rev3)
  R1 = Resistor [tolerance=±5% resistance=10k package=THT]
  LED1 = LED - 5mm [color="Red (633nm)" package="5 mm [THT]"]
  R2 = Resistor [tolerance=±5% resistance=100 package=THT]
  S1 = Pushbutton [package="[THT]"]

nets:
  N1: Part2.D9_PWM, LED1.anode
  N2: Part2.D10_PWM/SS, R1.Pin_0, S1.Pin_3, S1.Pin_4
  N3: Part2.GND, R1.Pin_1, R2.Pin_1
  N4: Part2.5V, S1.Pin_1, S1.Pin_2
  N5: LED1.cathode, R2.Pin_0
